// Logisim project 4BitAdder.circ as structural Verilog: 1 circuit, main circuit main
module main (
  input  X0,
  input  X2,
  input  X1,
  input  Y0,
  input  Y2,
  input  Y1,
  output CarryOut,
  output Sum2,
  output Sum1,
  output Sum0
);

  wire fulladder_1_cout, halfadder_1_carry;

  HalfAdder halfadder_1 (.X(X0), .Y(Y0), .Carry(halfadder_1_carry), .Sum(Sum0));
  FullAdder fulladder_1 (.Cin(halfadder_1_carry), .X(Y1), .Y(X1), .Cout(fulladder_1_cout), .Sum(Sum1));
  FullAdder fulladder_2 (.Cin(fulladder_1_cout), .X(Y2), .Y(X2), .Cout(CarryOut), .Sum(Sum2));
endmodule
