// Logisim project Adders.circ as structural Verilog: 2 circuits, main circuit HalfAdder
module HalfAdder (
  input  X,
  input  Y,
  output Carry,
  output Sum
);

  wire and_2_out, and_3_out, not_1_out, not_2_out;

  not not_1 (not_1_out, Y);
  not not_2 (not_2_out, X);
  and and_1 (Carry, X, Y);
  and and_2 (and_2_out, not_1_out, X);
  and and_3 (and_3_out, not_2_out, Y);
  or or_1 (Sum, and_2_out, and_3_out);
endmodule

module FullAdder (
  input  Cin,
  input  X,
  input  Y,
  output Cout,
  output Sum
);

  wire and_1_out, and_2_out, and_3_out, and_4_out, and_5_out, and_6_out, and_7_out, not_1_out, not_2_out,
       not_3_out, not_4_out, not_5_out, not_6_out;

  and and_1 (and_1_out, Cin, X);
  and and_2 (and_2_out, Cin, Y);
  and and_3 (and_3_out, X, Y);
  not not_1 (not_1_out, X);
  not not_2 (not_2_out, Cin);
  not not_3 (not_3_out, Cin);
  and and_4 (and_4_out, Cin, not_1_out, not_4_out);
  not not_4 (not_4_out, Y);
  and and_5 (and_5_out, not_2_out, X, not_5_out);
  not not_5 (not_5_out, Y);
  not not_6 (not_6_out, X);
  and and_6 (and_6_out, not_3_out, not_6_out, Y);
  and and_7 (and_7_out, Cin, X, Y);
  or or_1 (Cout, and_1_out, and_2_out, and_3_out);
  or or_2 (Sum, and_4_out, and_5_out, and_6_out, and_7_out);
endmodule
