// Logisim project CacheMemory.circ as structural Verilog: 2 circuits, main circuit main
module main (
  input  [5:0] in_1,
  input  [3:0] in_2,
  input  [3:0] in_3,
  input  [3:0] in_4,
  input  [3:0] in_5,
  output CacheMiss,
  output [3:0] out_7
);

  wire and_1_out, and_2_out, and_3_out, and_4_out, and_5_out, and_6_out, and_7_out, and_8_out,
       equal4_1_equal, equal4_2_equal, equal4_3_equal, equal4_4_equal, not_1_out;

  not not_1 (not_1_out, 1'b1);
  and and_1 (and_1_out, equal4_1_equal, not_1_out);
  and and_2 (and_2_out, equal4_1_equal, not_1_out);
  and and_3 (and_3_out, not_1_out, equal4_2_equal);
  and and_4 (and_4_out, 1'b1, equal4_2_equal);
  or or_1 (out_7[3], and_1_out, and_3_out, and_5_out, and_7_out);
  and and_5 (and_5_out, 1'b1, equal4_3_equal);
  and and_6 (and_6_out, not_1_out, equal4_3_equal);
  Equal4 equal4_1 (.First_Nibble(in_1[5:2]), .Second_Nibble(in_2), .Equal(equal4_1_equal));
  Equal4 equal4_2 (.First_Nibble(in_1[5:2]), .Second_Nibble(in_3), .Equal(equal4_2_equal));
  Equal4 equal4_3 (.First_Nibble(in_1[5:2]), .Second_Nibble(in_4), .Equal(equal4_3_equal));
  Equal4 equal4_4 (.First_Nibble(in_1[5:2]), .Second_Nibble(in_5), .Equal(equal4_4_equal));
  and and_7 (and_7_out, 1'b1, equal4_4_equal);
  and and_8 (and_8_out, 1'b1, equal4_4_equal);
  or or_2 (out_7[2], and_2_out, and_4_out, and_6_out, and_8_out);
  nor nor_1 (CacheMiss, equal4_1_equal, equal4_2_equal, equal4_3_equal, equal4_4_equal);

  assign out_7[1:0] = in_1[1:0];
endmodule

module Equal4 (
  input  [3:0] First_Nibble,
  input  [3:0] Second_Nibble,
  output Equal
);

  wire xnor_1_out, xnor_2_out, xnor_3_out, xnor_4_out;

  xnor xnor_1 (xnor_1_out, First_Nibble[0], Second_Nibble[0]);
  xnor xnor_2 (xnor_2_out, First_Nibble[1], Second_Nibble[1]);
  and and_1 (Equal, xnor_1_out, xnor_2_out, xnor_3_out, xnor_4_out);
  xnor xnor_3 (xnor_3_out, First_Nibble[2], Second_Nibble[2]);
  xnor xnor_4 (xnor_4_out, First_Nibble[3], Second_Nibble[3]);
endmodule
