// Logisim project Decoder.circ as structural Verilog: 1 circuit, main circuit main
module main (
  input  in_1,
  input  in_2,
  input  in_3,
  input  in_4,
  input  Enable,
  input  in_6,
  input  in_7,
  output output0,
  output output1,
  output output2,
  output output3,
  output output4,
  output output5,
  output output6,
  output output7,
  output output0_2,
  output output1_2,
  output output2_2,
  output output3_2
);

  wire not_1_out, not_2_out, not_3_out, not_4_out;

  Decoder #(.select(3)) decoder_1 (
    .out0(output0), .out1(output1), .out2(output2), .out3(output3), .out4(output4), .out5(output5),
    .out6(output6), .out7(output7), .sel({in_2, in_3, in_4}), .en(in_1));
  not not_1 (not_1_out, in_6);
  not not_2 (not_2_out, in_7);
  not not_3 (not_3_out, in_6);
  not not_4 (not_4_out, in_7);
  and and_1 (output0_2, Enable, not_1_out, not_2_out);
  and and_2 (output1_2, Enable, not_3_out, in_7);
  and and_3 (output2_2, Enable, in_6, not_4_out);
  and and_4 (output3_2, Enable, in_6, in_7);

  // Notes on the sheet:
  //   Enable
  //   address bits
  //   address bits
  //   3-bit decoder
  //   2-bit decoder
endmodule
