// Logisim project IncrementingRegister.circ as structural Verilog: 1 circuit, main circuit IncrementingRegister
module IncrementingRegister (
  input  [4:0] PCinput,
  input  Increment,
  input  in_3,
  output [4:0] PCoutput
);

  wire not_1_out;
  wire [4:0] adder_1_out, bitselector_1_out;

  not not_1 (not_1_out, Increment);
  BitSelector #(.width(10), .group(5)) bitselector_1 (
    .in({PCinput, adder_1_out}), .out(bitselector_1_out), .sel(not_1_out));
  Register #(.width(5)) register_1 (.D(bitselector_1_out), .Q(PCoutput), .clk(in_3));  // open: en, clr
  Adder #(.width(5)) adder_1 (.a(PCoutput), .b({5{1'b0}}), .out(adder_1_out), .cin(1'b1));  // open: cout
endmodule
