// Logisim project MemoryLayout.circ as structural Verilog: 1 circuit, main circuit main
module main (
  input  [7:0] Data_In,
  input  [4:0] Address,
  input  Clock,
  input  In_0__Out_1,
  input  Clear,
  output [7:0] Data_Out
);

  wire not_1_out;
  wire [7:0] ram_1_data;

  RAM #(.addrWidth(5), .dataWidth(8)) ram_1 (
    .addr(Address), .data(ram_1_data), .sel(1'b1), .clk(Clock), .ld(In_0__Out_1), .clr(Clear));
  assign ram_1_data = not_1_out ? Data_In : 8'bz;  // Controlled_Buffer controlled_buffer_1
  assign Data_Out = In_0__Out_1 ? ram_1_data : 8'bz;  // Controlled_Buffer controlled_buffer_2
  not not_1 (not_1_out, In_0__Out_1);
endmodule
