// Logisim project ThreeStateDevice.circ as structural Verilog: 1 circuit, main circuit main
module main (
  input  [7:0] In1,
  input  [7:0] In2,
  input  Select,
  input  Out,
  output [7:0] out_5
);

  wire [7:0] bitselector_1_out;

  BitSelector #(.width(16), .group(8)) bitselector_1 (.in({In2, In1}), .out(bitselector_1_out), .sel(Select));
  assign out_5 = Out ? bitselector_1_out : 8'bz;  // Controlled_Buffer controlled_buffer_1
endmodule
