// Logisim project TwoBitCounter.circ as structural Verilog: 1 circuit, main circuit TwoBitCounter
module TwoBitCounter (
  input  Clock,
  input  Clear,
  output [1:0] out_3
);

  wire not_1_out;
  wire [1:0] adder_1_out, register_1_q;

  Register #(.width(2)) register_1 (.D(out_3), .Q(register_1_q), .clk(Clock), .clr(Clear));  // open: en
  Adder #(.width(2)) adder_1 (.a(2'b01), .b(register_1_q), .out(adder_1_out));  // open: cin, cout
  not not_1 (not_1_out, Clock);
  Register #(.width(2)) register_2 (.D(adder_1_out), .Q(out_3), .clk(not_1_out), .clr(Clear));  // open: en
endmodule
