// Logisim project duh.circ as structural Verilog: 3 circuits, main circuit main
module main (
  input  [3:0] in_1,
  input  [3:0] in_2,
  output [1:0] out_3
);

  wire [3:0] duhduh_1_out_3;

  duhduh duhduh_1 (.duhduh(in_1), .in_2(in_2), .out_3(duhduh_1_out_3));
  duh duh_1 (.in_1(duhduh_1_out_3), .out_2(out_3));

  // Notes on the sheet:
  //   Then main used
  //   This shows how to do subcircuits.
  //   Double-click on them to see them.
  //   duh and duhduh were created first.
  //   both of them - a duduh feeding into a duh.
endmodule

module duh (
  input  [3:0] in_1,
  output [1:0] out_2
);

  wire and_1_out, and_2_out;

  and and_1 (and_1_out, in_1[0], in_1[1]);
  and and_2 (and_2_out, in_1[2], in_1[3]);
  or or_1 (out_2[0], and_1_out, and_2_out);

  assign out_2[1] = in_1[3];

  // Notes on the sheet:
  //   duh
endmodule

module duhduh (
  input  [3:0] duhduh,
  input  [3:0] in_2,
  output [3:0] out_3
);

  duh duh_1 (.in_1(duhduh), .out_2(out_3[1:0]));
  duh duh_2 (.in_1(in_2), .out_2(out_3[3:2]));
endmodule
