// Logisim project memoryLayout2.circ as structural Verilog: 1 circuit, main circuit main
module main (
  input  Select,
  input  In_0__Out_1,
  input  [1:0] Input,
  input  [1:0] Address,
  input  Clock,
  output [1:0] out_6
);

  wire and_1_out, and_2_out, and_3_out, and_4_out, and_5_out, and_6_out, and_7_out, and_8_out, and_9_out,
       and_10_out, and_11_out, and_12_out, and_13_out, and_14_out, and_15_out, and_16_out, and_17_out,
       and_18_out, d_ff_1_q, d_ff_2_q, d_ff_3_q, d_ff_4_q, d_ff_5_q, d_ff_6_q, d_ff_7_q, d_ff_8_q, not_1_out,
       not_2_out, not_3_out, not_4_out;
  wire [1:0] controlled_buffer_1_out, controlled_buffer_2_out, or_1_out;

  not not_1 (not_1_out, In_0__Out_1);
  and and_1 (and_1_out, not_1_out, Select);
  assign controlled_buffer_1_out = and_1_out ? Input : 2'bz;  // Controlled_Buffer controlled_buffer_1
  not not_2 (not_2_out, In_0__Out_1);
  not not_3 (not_3_out, Address[1]);
  not not_4 (not_4_out, Address[0]);
  and and_2 (and_2_out, not_3_out, not_4_out);
  and and_3 (and_3_out, not_3_out, Address[0]);
  and and_4 (and_4_out, not_4_out, Address[1]);
  and and_5 (and_5_out, Address[1], Address[0]);
  and and_6 (and_6_out, not_2_out, and_2_out, Clock);
  and and_7 (and_7_out, not_2_out, and_3_out, Clock);
  and and_8 (and_8_out, Clock, and_4_out, not_2_out);
  and and_9 (and_9_out, Clock, and_5_out, not_2_out);
  D_Flip_Flop d_ff_1 (.clk(and_6_out), .D(controlled_buffer_1_out[1]), .Q(d_ff_1_q));  // open: Qn, preset, en, reset
  D_Flip_Flop d_ff_2 (.clk(and_7_out), .D(controlled_buffer_1_out[1]), .Q(d_ff_2_q));  // open: Qn, preset, en, reset
  D_Flip_Flop d_ff_3 (.clk(and_8_out), .D(controlled_buffer_1_out[1]), .Q(d_ff_3_q));  // open: Qn, preset, en, reset
  D_Flip_Flop d_ff_4 (.clk(and_9_out), .D(controlled_buffer_1_out[1]), .Q(d_ff_4_q));  // open: Qn, preset, en, reset
  D_Flip_Flop d_ff_5 (.clk(and_6_out), .D(controlled_buffer_1_out[0]), .Q(d_ff_5_q));  // open: Qn, preset, en, reset
  and and_10 (and_10_out, d_ff_1_q, and_2_out);
  D_Flip_Flop d_ff_6 (.clk(and_7_out), .D(controlled_buffer_1_out[0]), .Q(d_ff_6_q));  // open: Qn, preset, en, reset
  and and_11 (and_11_out, d_ff_2_q, and_3_out);
  D_Flip_Flop d_ff_7 (.clk(and_8_out), .D(controlled_buffer_1_out[0]), .Q(d_ff_7_q));  // open: Qn, preset, en, reset
  and and_12 (and_12_out, d_ff_3_q, and_4_out);
  D_Flip_Flop d_ff_8 (.clk(and_9_out), .D(controlled_buffer_1_out[0]), .Q(d_ff_8_q));  // open: Qn, preset, en, reset
  and and_13 (and_13_out, d_ff_4_q, and_5_out);
  and and_14 (and_14_out, d_ff_5_q, and_2_out);
  and and_15 (and_15_out, d_ff_6_q, and_3_out);
  and and_16 (and_16_out, d_ff_7_q, and_4_out);
  and and_17 (and_17_out, d_ff_8_q, and_5_out);
  or or_1 (or_1_out[0], and_14_out, and_15_out, and_16_out, and_17_out);
  and and_18 (and_18_out, In_0__Out_1, Select);
  assign controlled_buffer_2_out = and_18_out ? or_1_out : 2'bz;  // Controlled_Buffer controlled_buffer_2
  or or_2 (or_1_out[1], and_10_out, and_11_out, and_12_out, and_13_out);
  Register #(.width(2)) \output  (.D(controlled_buffer_2_out), .Q(out_6), .clk(Clock));  // open: en, clr
endmodule
