// Logisim project Multiplexors.circ as structural Verilog: 1 circuit, main circuit main
module main (
  input  [1:0] in_1,
  input  on_off,
  input  in_3,
  input  in_4,
  input  in_5,
  input  input_bit,
  input  in_7,
  input  in_8,
  output [1:0] out_9,
  output [1:0] out_10,
  output [1:0] out_11,
  output [1:0] out_12,
  output [1:0] out_13,
  output [1:0] out_14,
  output [1:0] out_15,
  output [1:0] selected_output,
  output Output0,
  output Output1,
  output Output2,
  output Output3
);

  wire not_1_out, not_2_out, not_3_out, not_4_out;

  Demultiplexer #(.select(3), .width(2)) demultiplexer_1 (
    .out0(out_9), .out1(out_10), .out2(out_11), .out3(out_12), .out4(out_13), .out5(out_14), .out6(out_15),
    .out7(selected_output), .in(in_1), .sel({in_3, in_4, in_5}), .en(on_off));
  not not_1 (not_1_out, in_7);
  not not_2 (not_2_out, in_8);
  not not_3 (not_3_out, in_7);
  not not_4 (not_4_out, in_8);
  and and_1 (Output0, not_1_out, not_2_out, input_bit);
  and and_2 (Output1, input_bit, in_8, not_3_out);
  and and_3 (Output2, not_4_out, input_bit, in_7);
  and and_4 (Output3, input_bit, in_7, in_8);

  // Notes on the sheet:
  //   address bits
  //   input bits
  //   address bits
  //   selected output
  //   4x2 multiplexor
  //   2x1 multiplexor
endmodule
