// Logisim project ThreeBitCounter.circ as structural Verilog: 1 circuit, main circuit main
module main (
  input  Clock,
  input  Clear,
  output _0,
  output _1,
  output _2,
  output _3,
  output _4,
  output _5,
  output _6,
  output _7
);

  wire [2:0] Counter_q;

  Counter #(.width(3), .max('h7)) Counter (
    .count(Clock), .Q(Counter_q), .clk(Clock), .clr(Clear));  // open: load, D, carry
  Decoder #(.select(3)) decoder_1 (
    .out0(_0), .out1(_1), .out2(_2), .out3(_3), .out4(_4), .out5(_5), .out6(_6), .out7(_7), .sel(Counter_q));  // open: en
endmodule
