// Logisim project TwoBitMultiplier.circ as structural Verilog: 1 circuit, main circuit main
module main (
  input  X1,
  input  X0,
  input  Y1,
  input  Y0,
  output P3,
  output P2,
  output P1,
  output P0
);

  wire and_2_out, and_3_out, and_4_out, and_5_out, and_6_out, and_7_out, not_1_out, not_2_out, not_3_out,
       not_4_out;

  not not_1 (not_1_out, X1);
  not not_2 (not_2_out, Y1);
  not not_3 (not_3_out, X0);
  not not_4 (not_4_out, Y0);
  and and_1 (P3, X1, X0, Y0, Y1);
  and and_2 (and_2_out, X1, Y1, not_4_out);
  and and_3 (and_3_out, X1, not_3_out, Y1);
  and and_4 (and_4_out, not_1_out, X0, Y1);
  and and_5 (and_5_out, X0, Y1, not_4_out);
  and and_6 (and_6_out, X1, not_2_out, Y0);
  and and_7 (and_7_out, X1, not_3_out, Y0);
  and and_8 (P0, Y0, X0);
  or or_1 (P2, and_2_out, and_3_out);
  or or_2 (P1, and_4_out, and_5_out, and_6_out, and_7_out);
endmodule
