// Logisim project JPOS.circ as structural Verilog: 1 circuit, main circuit main
module main (
  input  [2:0] Counter,
  input  ZeroPOS,
  input  [7:0] IR,
  output PCout,
  output READ,
  output MARin,
  output MDRout,
  output IRin,
  output IRout,
  output PCin,
  output Reset_Counter,
  output [7:0] Address
);

  wire decoder_1_out2, decoder_1_out3, decoder_2_out1;

  // AND_Gate and_1 is placed but not wired
  Decoder #(.select(3)) decoder_1 (
    .out0(MARin), .out1(IRin), .out2(decoder_1_out2), .out3(decoder_1_out3), .sel(Counter), .en(1'b1));  // open: out4, out5, out6, out7
  Decoder #(.select(3)) decoder_2 (
    .out1(decoder_2_out1), .sel(IR[7:5]), .en(ZeroPOS));  // open: out0, out2, out3, out4, out5, out6, out7
  and and_2 (IRout, decoder_1_out2, decoder_2_out1);
  and and_3 (Reset_Counter, decoder_1_out3, decoder_2_out1);

  assign Address = IR;
  assign MDRout = IRin;
  assign PCin = IRout;
  assign PCout = MARin;
  assign READ = MARin;
endmodule
