// Logisim project STOR.circ as structural Verilog: 1 circuit, main circuit main
module main (
  input  [2:0] Counter,
  input  [7:0] IR,
  output PCout,
  output READ,
  output MARin,
  output MDROut,
  output IRin,
  output ACCout,
  output MDRin,
  output IRout,
  output MARin_2,
  output WRITE,
  output Reset_Counter,
  output [7:0] Address
);

  wire decoder_1_out2, decoder_1_out3, decoder_1_out4, decoder_2_out5;

  Decoder #(.select(3)) decoder_1 (
    .out0(MARin), .out1(IRin), .out2(decoder_1_out2), .out3(decoder_1_out3), .out4(decoder_1_out4),
    .sel(Counter), .en(1'b1));  // open: out5, out6, out7
  Decoder #(.select(3)) decoder_2 (
    .out5(decoder_2_out5), .sel(IR[7:5]), .en(1'b1));  // open: out0, out1, out2, out3, out4, out6, out7
  and and_1 (ACCout, decoder_1_out2, decoder_2_out5);
  and and_2 (IRout, decoder_1_out3, decoder_2_out5);
  and and_3 (Reset_Counter, decoder_1_out4, decoder_2_out5);

  assign Address = IR;
  assign MARin_2 = IRout;
  assign MDRin = ACCout;
  assign MDROut = IRin;
  assign PCout = MARin;
  assign READ = MARin;
  assign WRITE = IRout;
endmodule
