// Logisim project MAR.circ as structural Verilog: 1 circuit, main circuit main
module main (
  input  [7:0] Address,
  input  MARin,
  output [7:0] out_3
);

  assign out_3 = MARin ? Address : 8'bz;  // Controlled_Buffer controlled_buffer_1
endmodule
