// Logisim project HALT.circ as structural Verilog: 1 circuit, main circuit main
module main (
  input  [2:0] in_1,
  input  [7:0] IR,
  output PCout,
  output READ,
  output MARIn,
  output MDRout,
  output IRin,
  output CLOCK_OFF,
  output Reset_Counter,
  output [7:0] Address
);

  wire decoder_1_out2, decoder_1_out3, decoder_2_out0;

  Decoder #(.select(3)) decoder_1 (
    .out0(MARIn), .out1(IRin), .out2(decoder_1_out2), .out3(decoder_1_out3), .sel(in_1), .en(1'b1));  // open: out4, out5, out6, out7
  Decoder #(.select(3)) decoder_2 (
    .out0(decoder_2_out0), .sel(IR[7:5]), .en(1'b1));  // open: out1, out2, out3, out4, out5, out6, out7
  and and_1 (CLOCK_OFF, decoder_1_out2, decoder_2_out0);
  and and_2 (Reset_Counter, decoder_1_out3, decoder_2_out0);

  assign Address = IR;
  assign MDRout = IRin;
  assign PCout = MARIn;
  assign READ = MARIn;
endmodule
