// Logisim project JZER.circ as structural Verilog: 1 circuit, main circuit main
module main (
  input  [2:0] Counter,
  input  ZeroFlag,
  input  [7:0] IR,
  output PCout,
  output READ,
  output MARin,
  output MDRout,
  output IRin,
  output IRout,
  output PCin,
  output Reset_Counter,
  output [7:0] Address
);

  wire decoder_1_out2, decoder_1_out3, decoder_2_out2;

  Decoder #(.select(3)) decoder_1 (
    .out0(MARin), .out1(IRin), .out2(decoder_1_out2), .out3(decoder_1_out3), .sel(Counter), .en(1'b1));  // open: out4, out5, out6, out7
  Decoder #(.select(3)) decoder_2 (
    .out2(decoder_2_out2), .sel(IR[7:5]), .en(ZeroFlag));  // open: out0, out1, out3, out4, out5, out6, out7
  and and_1 (IRout, decoder_1_out2, decoder_2_out2);
  and and_2 (Reset_Counter, decoder_1_out3, decoder_2_out2);

  assign Address = IR;
  assign MDRout = IRin;
  assign PCin = IRout;
  assign PCout = MARin;
  assign READ = MARin;
endmodule
