// Logisim project Zurn8BitOSMainInstructionRegister.circ as structural Verilog: 1 circuit, main circuit main
// InstuctionRegisters
module main (
  input  [7:0] IR,
  input  [2:0] Counter,
  input  JZER,
  input  JPOS,
  output PCout,
  output IRout,
  output MDRout,
  output READ,
  output ACCout,
  output MDRin,
  output ACCin,
  output WRITE,
  output ADD,
  output MARin,
  output SUB,
  output ALUout,
  output RESET,
  output CLOCKoff,
  output IRin,
  output [7:0] Address
);

  wire addACCin, addALUout, addIRin, addIRout, addMARin, addMARin2, addMDRout, addPCout, addREAD, addREAD2,
       addRESET, haltIRin, haltMARin, haltMDRout, haltPCout, haltREAD, haltRESET, jposIRin, jposIRout,
       jposMARin, jposMDRout, jposPCinc, jposPCout, jposREAD, jposRESET, jumpIRin, jumpIRout, jumpMARin,
       jumpMDRout, jumpPCinc, jumpPCout, jumpREAD, jumpRESET, jzerIRin, jzerIRout, jzerMARin, jzerMDRout,
       jzerPCinc, jzerPCout, jzerREAD, jzerRESET, loadACCin, loadIRin, loadIRout, loadMARin, loadMARin2,
       loadMDRout, loadMDRout2, loadPCout, loadREAD, loadREAD2, loadRESET, or_2_out, or_4_out, or_5_out,
       or_7_out, storIRin, storIRout, storMARin, storMARin2, storMDRout, storPCout, storREAD, storRESET,
       subACCin, subALUout, subIRin, subIRout, subMARin, subMARin2, subMDRout, subPCout, subREAD, subREAD2,
       subRESET;

  ADD_main u_Add (
    .Counter(Counter), .IR(IR), .PCout(addPCout), .READ(addREAD), .MARin(addMARin), .MDRout(addMDRout),
    .IRin(addIRin), .IRout(addIRout), .MARin_2(addMARin2), .READ_2(addREAD2), .ADD(ADD), .ALUout(addALUout),
    .ACCin(addACCin), .Reset_Counter(addRESET), .Address(Address));
  SUB_main u_Sub (
    .Counter(Counter), .IR(IR), .PCout(subPCout), .READ(subREAD), .MARin(subMARin), .MDRout(subMDRout),
    .IRin(subIRin), .IRout(subIRout), .MARin_2(subMARin2), .READ_2(subREAD2), .SUBTRACT(SUB),
    .ALUout(subALUout), .ACCin(subACCin), .Reset_Counter(subRESET), .Address(Address));
  Load_main Load (
    .Counter(Counter), .IR(IR), .PCout(loadPCout), .READ(loadREAD), .MARin(loadMARin), .MDRout(loadMDRout),
    .IRin(loadIRin), .IRout(loadIRout), .MARin_2(loadMARin2), .READ_2(loadREAD2), .MDRout_2(loadMDRout2),
    .ACCin(loadACCin), .Reset_Counter(loadRESET), .Address(Address));
  STOR_main Stor (
    .Counter(Counter), .IR(IR), .PCout(storPCout), .READ(storREAD), .MARin(storMARin), .MDROut(storMDRout),
    .IRin(storIRin), .ACCout(ACCout), .MDRin(MDRin), .IRout(storIRout), .MARin_2(storMARin2), .WRITE(WRITE),
    .Reset_Counter(storRESET), .Address(Address));
  Jump_main Jump (
    .Counter(Counter), .IR(IR), .PCout(jumpPCout), .READ(jumpREAD), .MARin(jumpMARin), .MDRout(jumpMDRout),
    .IRin(jumpIRin), .IRout(jumpIRout), .PCin(jumpPCinc), .Reset_Counter(jumpRESET), .Address(Address));
  JZER_main JZERO (
    .Counter(Counter), .IR(IR), .PCout(jzerPCout), .READ(jzerREAD), .MARin(jzerMARin), .MDRout(jzerMDRout),
    .IRin(jzerIRin), .IRout(jzerIRout), .PCin(jzerPCinc), .Reset_Counter(jzerRESET), .ZeroFlag(JZER),
    .Address(Address));
  // JPOS_main JPOS: pin names not known; wires that end beside it: Counter, IR, JPOS, jposPCout, jposREAD, jposMARin, jposMDRout, jposIRin, jposIRout, jposPCinc, jposRESET, Address
  HALT_main Halt (
    .in_1(Counter), .IR(IR), .PCout(haltPCout), .READ(haltREAD), .MARIn(haltMARin), .MDRout(haltMDRout),
    .IRin(haltIRin), .CLOCK_OFF(CLOCKoff), .Reset_Counter(haltRESET), .Address(Address));
  or or_1 (PCout, addPCout, subPCout, loadPCout, storPCout, jumpPCout, jzerPCout, jposPCout, haltPCout);
  or or_2 (or_2_out, addREAD, subREAD, loadREAD, storREAD, jumpREAD, jzerREAD, jposREAD, haltREAD);
  or or_3 (READ, or_2_out, or_4_out);
  or or_4 (or_4_out, addREAD2, subREAD2, loadREAD2);
  or or_5 (or_5_out, addMARin, subMARin, loadMARin, storMARin, jumpMARin, jzerMARin, jposMARin, haltMARin);
  or or_6 (MARin, or_5_out, or_7_out);
  or or_7 (or_7_out, addMARin2, subMARin2, loadMARin2, storMARin2);
  or or_8 (IRin, addIRin, subIRin, loadIRin, storIRin, jumpIRin, jzerIRin, jposIRin, haltIRin);
  or or_9 (ACCin, addACCin, subACCin, loadACCin);
  or or_10 (IRout, addIRout, subIRout, loadIRout, storIRout, jumpIRout, jzerIRout, jposIRout);
  or or_11 (MDRout, addMDRout, subMDRout, loadMDRout, storMDRout, jumpMDRout, jzerMDRout, jposMDRout, haltMDRout);
  or or_12 (ALUout, addALUout, subALUout);
  or or_13 (RESET, addRESET, subRESET, loadRESET, storRESET, jumpRESET, jzerRESET, jposRESET, haltRESET);

  // Other names for the same wires on the sheet: haltCLOCKoff = CLOCKoff; storACCout = ACCout; storMDRin = MDRin;
  //   storWRITE = WRITE
endmodule
