// Logisim project InsturctionRegister.circ as structural Verilog: 1 circuit, main circuit main
module main (
  input  IRout,
  input  [7:0] Address,
  input  IRin,
  output [7:0] IRoutAddress,
  output [7:0] out_5
);

  assign IRoutAddress = IRout ? out_5 : 8'bz;  // Controlled_Buffer controlled_buffer_1
  Register register_1 (.D(Address), .en(1'b1), .Q(out_5), .clk(IRin));  // open: clr
endmodule
