// Logisim project Zurn8BitOSProjectMain.circ as structural Verilog: 1 circuit, main circuit main
module main (
  input  [7:0] in_1,
  input  ZeroFlag,
  input  PositiveFlag,
  output [7:0] out_4,
  output [7:0] out_5,
  output [7:0] out_6
);

  wire ACCin, ACCout, ADD, ALUout, Clock, ClockOff, IRin, IRout, MARin, MDRin, MDRout, PCout, READ, RESET,
       SUB, WRITE;
  wire [2:0] counter_1_q;
  wire [7:0] main_1_out_3;

  InsturctionRegister_main IR (.IRout(IRout), .Address(out_4), .IRin(IRin), .IRoutAddress(out_6));  // open: out_5
  Counter #(.width(3), .max('h6)) counter_1 (.Q(counter_1_q), .clk(Clock), .clr(RESET));  // open: load, D, count, carry
  Clock clock_1 (.out(Clock));
  MAR_main main_1 (.Address(out_6), .MARin(MARin), .out_3(main_1_out_3));
  Zurn8BitOSMainInstructionRegister_main main_2 (
    .IR(in_1), .Counter(counter_1_q), .JZER(ZeroFlag), .JPOS(PositiveFlag), .PCout(PCout), .IRout(IRout),
    .MDRout(MDRout), .READ(READ), .ACCout(ACCout), .MDRin(MDRin), .ACCin(ACCin), .WRITE(WRITE), .ADD(ADD),
    .MARin(MARin), .SUB(SUB), .ALUout(ALUout), .RESET(RESET), .CLOCKoff(ClockOff), .IRin(IRin),
    .Address(out_4));
  RAM ram_1 (.addr(main_1_out_3), .data(out_5), .ld(MARin));  // open: sel, clk, clr

  // Other names for the same wires on the sheet: Address[7:0] = out_4
endmodule
